// Logisim project alu.circ as structural Verilog: 3 circuits, main circuit alu
module alu (
  input  [31:0] A,
  input  [31:0] B,
  input  [3:0] ALUSel,
  output [31:0] Result
);

  wire isNegative, slt0;
  wire [0:0] adder_2_cout;
  wire [31:0] add0, and0, divu0, mul0, mulh0, mulhNegative, mulhu0, multiplier_1_out, not_1_out, not_2_out,
       or0, positiveA, positiveB, positiveHighBits, positiveLowBits, remu0, sll0, sra0, srl0, sub0, xor0;

  Adder #(.width(32)) adder_1 (.a(A), .b(B), .out(add0));  // open: cin, cout
  assign and0 = A & B;  // AND_Gate and_1, 32 bits wide
  assign or0 = A | B;  // OR_Gate or_1, 32 bits wide
  assign xor0 = A ^ B;  // XOR_Gate xor_1, 32 bits wide
  Shifter #(.width(32), .shift("lr")) shifter_1 (.in(A), .\dist (B[4:0]), .out(srl0));
  Shifter #(.width(32), .shift("ar")) shifter_2 (.in(A), .\dist (B[4:0]), .out(sra0));
  Shifter #(.width(32)) shifter_3 (.in(A), .\dist (B[4:0]), .out(sll0));
  Comparator #(.width(32)) comparator_1 (.a(A), .b(B), .lt(slt0));  // open: gt, eq
  Divider #(.width(32)) divider_1 (.a(A), .b(B), .out(divu0));  // open: upper, rem
  Multiplier #(.width(32)) multiplier_1 (.a(divu0), .b(B), .out(multiplier_1_out));  // open: cin, cout
  Multiplier #(.width(32)) multiplier_2 (.a(A), .b(B), .out(mul0), .cout(mulhu0));  // open: cin
  Subtractor #(.width(32)) subtractor_1 (.a(A), .b(B), .out(sub0));  // open: bin, bout
  Subtractor #(.width(32)) subtractor_2 (.a(A), .b(multiplier_1_out), .out(remu0));  // open: bin, bout
  Multiplexer #(.select(4), .width(32), .enable("false")) multiplexer_1 (
    .in0(add0), .in1(and0), .in2(or0), .in3(xor0), .in4(srl0), .in5(sra0), .in6(sll0),
    .in7({{31{1'b0}}, slt0}), .in8(divu0), .in9(remu0), .in10(mul0), .in11(mulhu0), .in12(sub0), .in13(B),
    .in14(mulh0), .out(Result), .sel(ALUSel));  // open: in15
  xor xor_2 (isNegative, A[31], B[31]);
  getPositive getpositive_1 (.in_1(A), .out_2(positiveA));
  getPositive getpositive_2 (.in_1(B), .out_2(positiveB));
  Multiplier #(.width(32)) multiplier_3 (
    .a(positiveA), .b(positiveB), .out(positiveLowBits), .cout(positiveHighBits));  // open: cin
  assign not_1_out = ~positiveLowBits;  // NOT_Gate not_1, 32 bits wide
  assign not_2_out = ~positiveHighBits;  // NOT_Gate not_2, 32 bits wide
  Multiplexer #(.width(32), .enable("false")) multiplexer_2 (
    .in0(positiveHighBits), .in1(mulhNegative), .out(mulh0), .sel(isNegative));
  Adder #(.width(32)) adder_2 (.a(not_1_out), .b(32'h1), .cout(adder_2_cout[0]));  // open: out, cin
  Adder #(.width(32)) adder_3 (
    .a({{31{1'b0}}, adder_2_cout[0]}), .b(not_2_out), .out(mulhNegative));  // open: cin, cout

  // Other names for the same wires on the sheet: bsel[31:0] = B

  // Notes on the sheet:
  //   INPUTS to your circuit
  //   Get the high bits in positive result's complement
  //   OUTPUT from your circuit
endmodule

module getComplement (
  input  [31:0] in_1,
  output [31:0] out_2
);

  wire [31:0] not_1_out;

  assign not_1_out = ~in_1;  // NOT_Gate not_1, 32 bits wide
  Adder #(.width(32)) adder_1 (.a(not_1_out), .b(32'h1), .out(out_2));  // open: cin, cout
endmodule

module getPositive (
  input  [31:0] in_1,
  output [31:0] out_2
);

  wire [31:0] getcomplement_1_out_2;

  Multiplexer #(.width(32), .enable("false")) multiplexer_1 (
    .in0(in_1), .in1(getcomplement_1_out_2), .out(out_2), .sel(in_1[31]));
  getComplement getcomplement_1 (.in_1(in_1), .out_2(getcomplement_1_out_2));
endmodule
