// Logisim project branch_comp.circ as structural Verilog: 1 circuit, main circuit branch_comp
module branch_comp (
  input  [31:0] rs1,
  input  [31:0] rs2,
  input  BrUn,
  output BrEq,
  output BrLt
);

  wire BrEq_Signed, BrEq_UnSigned, BrLt_Signed, BrLt_UnSigned;

  Comparator #(.width(32)) comparator_1 (.a(rs1), .b(rs2), .eq(BrEq_Signed), .lt(BrLt_Signed));  // open: gt
  Comparator #(.width(32), .mode("unsigned")) comparator_2 (
    .a(rs1), .b(rs2), .eq(BrEq_UnSigned), .lt(BrLt_UnSigned));  // open: gt
  Multiplexer #(.enable("false")) multiplexer_1 (.in0(BrEq_Signed), .in1(BrEq_UnSigned), .out(BrEq), .sel(BrUn));
  Multiplexer #(.enable("false")) multiplexer_2 (.in0(BrLt_Signed), .in1(BrLt_UnSigned), .out(BrLt), .sel(BrUn));

  // Notes on the sheet:
  //   INPUTS to your circuit
  //   OUTPUT from your circuit
endmodule
