// Logisim project control_logic.circ as structural Verilog: 1 circuit, main circuit control_logic
module control_logic (
  input  [31:0] inst,
  input  BrEq,
  input  BrLt,
  output PCSel,
  output RegWEn,
  output [2:0] ImmSel,
  output BrUn,
  output ASel,
  output BSel,
  output [3:0] ALUSel,
  output MemRW,
  output [1:0] WBSel
);

  wire add0, add_mul_sub, addi, and0, and_1_out, and_2_out, and_3_out, and_4_out, andi, demultiplexer_2_out0,
       demultiplexer_7_out0, divu0, divu_srl_sra, isAuipc, isBeq, isBge, isBgeu, isBlt, isBne, isJal, isJalr,
       isLoad, isLui, isOpI, isR, isSB, mul0, mulh0, mulhu, needALU, needAnd, needBSel, needI, needOr,
       needPCPlus4, needRemu, needSll, needSlt, needSra, needSrl, needSub, needU, needXor, not_2_out,
       not_3_out, or0, or_9_out, or_10_out, ori, remu_and, sll0, sll_mulh, slli, slt, slti, sra0, srai, srl0,
       srli, srli_srai, xor0, xori;
  wire [1:0] multiplexer_7_out, multiplexer_9_out;
  wire [2:0] multiplexer_14_out, multiplexer_16_out, multiplexer_19_out, multiplexer_20_out;
  wire [3:0] multiplexer_1_out, multiplexer_2_out, multiplexer_3_out, multiplexer_4_out, multiplexer_5_out,
       multiplexer_6_out, multiplexer_8_out, multiplexer_10_out, multiplexer_12_out, multiplexer_13_out,
       multiplexer_15_out, multiplexer_17_out, multiplexer_18_out;

  Comparator #(.width(7)) comparator_1 (.a(inst[6:0]), .b(7'b0110011), .eq(isR));  // open: gt, lt
  Comparator #(.width(7)) comparator_2 (.a(inst[6:0]), .b(7'b0000011), .eq(isLoad));  // open: gt, lt
  Comparator #(.width(7)) comparator_3 (.a(inst[6:0]), .b(7'b0010011), .eq(isOpI));  // open: gt, lt
  Comparator #(.width(7)) comparator_4 (.a(inst[6:0]), .b(7'b0100011), .eq(MemRW));  // open: gt, lt
  Comparator #(.width(7)) comparator_5 (.a(inst[6:0]), .b(7'b1100011), .eq(isSB));  // open: gt, lt
  Comparator #(.width(7)) comparator_6 (.a(inst[6:0]), .b(7'b0010111), .eq(isAuipc));  // open: gt, lt
  Comparator #(.width(7)) comparator_7 (.a(inst[6:0]), .b(7'b0110111), .eq(isLui));  // open: gt, lt
  Comparator #(.width(7)) comparator_8 (.a(inst[6:0]), .b(7'b1101111), .eq(isJal));  // open: gt, lt
  Comparator #(.width(7)) comparator_9 (.a(inst[6:0]), .b(7'b1100111), .eq(isJalr));  // open: gt, lt
  Multiplexer #(.width(4), .enable("false")) multiplexer_1 (
    .in0(4'b0000), .in1(4'b0001), .out(multiplexer_1_out), .sel(needAnd));
  Multiplexer #(.width(4), .enable("false")) multiplexer_2 (
    .in0(multiplexer_1_out), .in1(4'b0010), .out(multiplexer_2_out), .sel(needOr));
  Demultiplexer #(.select(3), .enable("false")) demultiplexer_1 (
    .out0(isBeq), .out1(isBne), .out4(isBlt), .out5(isBge), .out6(BrUn), .out7(isBgeu), .in(isSB),
    .sel(inst[14:12]));  // open: out2, out3
  Multiplexer #(.width(4), .enable("false")) multiplexer_3 (
    .in0(multiplexer_2_out), .in1(4'b0011), .out(multiplexer_3_out), .sel(needXor));
  Multiplexer #(.width(4), .enable("false")) multiplexer_4 (
    .in0(multiplexer_3_out), .in1(4'b0100), .out(multiplexer_4_out), .sel(needSrl));
  or or_1 (ASel, isSB, isAuipc, isJal, isJalr);
  or or_2 (needALU, isR, isOpI, isAuipc);
  Multiplexer #(.width(4), .enable("false")) multiplexer_5 (
    .in0(multiplexer_4_out), .in1(4'b0101), .out(multiplexer_5_out), .sel(needSra));
  Multiplexer #(.width(4), .enable("false")) multiplexer_6 (
    .in0(multiplexer_5_out), .in1(4'b0110), .out(multiplexer_6_out), .sel(needSll));
  or or_3 (needSlt, slt, slti);
  not not_1 (BSel, isR);
  or or_4 (needPCPlus4, isJal, isJalr);
  Multiplexer #(.width(2), .enable("false")) multiplexer_7 (
    .in0(2'b11), .in1(2'b00), .out(multiplexer_7_out), .sel(needPCPlus4));
  Multiplexer #(.width(4), .enable("false")) multiplexer_8 (
    .in0(multiplexer_6_out), .in1(4'b0111), .out(multiplexer_8_out), .sel(needSlt));
  or or_5 (needI, isLoad, isOpI, isJalr);
  or or_6 (needU, isAuipc, isLui);
  Multiplexer #(.width(2), .enable("false")) multiplexer_9 (
    .in0(multiplexer_7_out), .in1(2'b01), .out(multiplexer_9_out), .sel(needALU));
  or or_7 (needSll, sll0, slli);
  Multiplexer #(.width(4), .enable("false")) multiplexer_10 (
    .in0(multiplexer_8_out), .in1(4'b1000), .out(multiplexer_10_out), .sel(divu0));
  Multiplexer #(.width(2), .enable("false")) multiplexer_11 (
    .in0(multiplexer_9_out), .in1(2'b10), .out(WBSel), .sel(isLoad));
  or or_8 (needBSel, MemRW, isLui);
  Multiplexer #(.width(4), .enable("false")) multiplexer_12 (
    .in0(multiplexer_10_out), .in1(4'b1001), .out(multiplexer_12_out), .sel(needRemu));
  Multiplexer #(.width(4), .enable("false")) multiplexer_13 (
    .in0(multiplexer_12_out), .in1(4'b1010), .out(multiplexer_13_out), .sel(mul0));
  or or_9 (or_9_out, isBlt, BrUn);
  or or_10 (or_10_out, isBge, isBgeu);
  Multiplexer #(.width(3), .enable("false")) multiplexer_14 (
    .in0(3'b000), .in1(3'b001), .out(multiplexer_14_out), .sel(needI));
  or or_11 (needSra, sra0, srai);
  Multiplexer #(.width(4), .enable("false")) multiplexer_15 (
    .in0(multiplexer_13_out), .in1(4'b1011), .out(multiplexer_15_out), .sel(mulhu));
  not not_2 (not_2_out, BrEq);
  not not_3 (not_3_out, BrLt);
  Multiplexer #(.width(3), .enable("false")) multiplexer_16 (
    .in0(multiplexer_14_out), .in1(3'b010), .out(multiplexer_16_out), .sel(MemRW));
  Multiplexer #(.width(4), .enable("false")) multiplexer_17 (
    .in0(multiplexer_15_out), .in1(4'b1100), .out(multiplexer_17_out), .sel(needSub));
  and and_1 (and_1_out, isBeq, BrEq);
  and and_2 (and_2_out, isBne, not_2_out);
  and and_3 (and_3_out, or_9_out, BrLt);
  and and_4 (and_4_out, or_10_out, not_3_out);
  Multiplexer #(.width(4), .enable("false")) multiplexer_18 (
    .in0(multiplexer_17_out), .in1(4'b1101), .out(multiplexer_18_out), .sel(needBSel));
  or or_12 (RegWEn, isR, isLoad, isOpI, isAuipc, isLui, isJal, isJalr);
  Multiplexer #(.width(3), .enable("false")) multiplexer_19 (
    .in0(multiplexer_16_out), .in1(3'b011), .out(multiplexer_19_out), .sel(isSB));
  Demultiplexer #(.enable("false")) demultiplexer_2 (
    .out0(demultiplexer_2_out0), .out1(sra0), .in(divu_srl_sra), .sel(inst[30]));
  or or_13 (needSrl, srl0, srli);
  or or_14 (PCSel, and_1_out, and_2_out, and_3_out, and_4_out);
  Multiplexer #(.width(3), .enable("false")) multiplexer_20 (
    .in0(multiplexer_19_out), .in1(3'b100), .out(multiplexer_20_out), .sel(needU));
  Demultiplexer #(.enable("false")) demultiplexer_3 (
    .out0(srl0), .out1(divu0), .in(demultiplexer_2_out0), .sel(inst[25]));
  Multiplexer #(.width(4), .enable("false")) multiplexer_21 (
    .in0(multiplexer_18_out), .in1(4'b1110), .out(ALUSel), .sel(mulh0));
  Multiplexer #(.width(3), .enable("false")) multiplexer_22 (
    .in0(multiplexer_20_out), .in1(3'b101), .out(ImmSel), .sel(isJal));
  or or_15 (needXor, xor0, xori);
  Demultiplexer #(.enable("false")) demultiplexer_4 (.out0(sll0), .out1(mulh0), .in(sll_mulh), .sel(inst[25]));
  Demultiplexer #(.select(3), .enable("false")) demultiplexer_5 (
    .out0(add_mul_sub), .out1(sll_mulh), .out2(slt), .out3(mulhu), .out4(xor0), .out5(divu_srl_sra),
    .out6(or0), .out7(remu_and), .in(isR), .sel(inst[14:12]));
  Demultiplexer #(.select(3), .enable("false")) demultiplexer_6 (
    .out0(addi), .out1(slli), .out2(slti), .out4(xori), .out5(srli_srai), .out6(ori), .out7(andi),
    .in(isOpI), .sel(inst[14:12]));  // open: out3
  or or_16 (needAnd, andi, and0);
  Demultiplexer #(.enable("false")) demultiplexer_7 (
    .out0(demultiplexer_7_out0), .out1(needSub), .in(add_mul_sub), .sel(inst[30]));
  Demultiplexer #(.enable("false")) demultiplexer_8 (.out0(srli), .out1(srai), .in(srli_srai), .sel(inst[30]));
  Demultiplexer #(.enable("false")) demultiplexer_9 (
    .out0(add0), .out1(mul0), .in(demultiplexer_7_out0), .sel(inst[25]));
  Demultiplexer #(.enable("false")) demultiplexer_10 (.out0(and0), .out1(needRemu), .in(remu_and), .sel(inst[25]));
  or or_17 (needOr, or0, ori);

  // Other names for the same wires on the sheet: opcode[6:0] = inst[6:0]; func3[2:0] = inst[14:12];
  //   rs1[4:0] = inst[19:15]; rs2[4:0] = inst[24:20]; func7[6:0] = inst[31:25]; func7_0 = inst[25];
  //   func7_5 = inst[30]; isBltu = BrUn; needDivu = divu0; needMem = isLoad; needMul = mul0; needMulh = mulh0;
  //   needMulhu = mulhu; isS = MemRW; needS = MemRW; needSB = isSB; needUJ = isJal; remu0 = needRemu; sub0 = needSub

  // Notes on the sheet:
  //   INPUTS to your circuit
  //   DON'T CHANGE THE LOCATIONS OF THE INPUTS AND OUTPUTS!
  //   OUTPUT from your circuit
endmodule
