// Logisim project cpu.circ as structural Verilog: 1 circuit, main circuit main
module main (
  input  [31:0] INSTRUCTION,
  input  CLOCK,
  output [31:0] PROGRAM_COUNTER,
  output [31:0] ra,
  output [31:0] sp,
  output [31:0] t0,
  output [31:0] t1,
  output [31:0] t2,
  output [31:0] s0,
  output [31:0] s1,
  output [31:0] a0
);

  wire ASel, BrEq, BrLt, BrUn, BSel, MemRW, PCSel, RegWEn;
  wire [1:0] WBSel;
  wire [2:0] ImmSel;
  wire [3:0] ALUSel;
  wire [31:0] A, adder_1_out, adder_2_out, ALU_result, B, immediate, INSTRUCTION_DELAY, multiplexer_1_out,
       multiplexer_2_out, PROGRAM_COUNTER_DELAY, ReadData, rs1Val, rs2Val, wb;

  control_logic control_logic_1 (
    .BSel(BSel), .BrUn(BrUn), .RegWEn(RegWEn), .ImmSel(ImmSel), .ASel(ASel), .PCSel(PCSel), .BrLt(BrLt),
    .BrEq(BrEq), .inst(INSTRUCTION_DELAY), .ALUSel(ALUSel), .MemRW(MemRW), .WBSel(WBSel));
  Adder #(.width(32)) adder_1 (.a(PROGRAM_COUNTER), .b(32'h4), .out(adder_1_out));  // open: cin, cout
  Multiplexer #(.width(32), .enable("false")) multiplexer_1 (
    .in0(adder_1_out), .in1(ALU_result), .out(multiplexer_1_out), .sel(PCSel));
  Register #(.width(32)) PC (.D(multiplexer_1_out), .clk(CLOCK), .Q(PROGRAM_COUNTER));  // open: en, clr
  imm_gen imm_gen_1 (.ImmSel(ImmSel), .inst(INSTRUCTION_DELAY), .imm(immediate));
  Multiplexer #(.width(32), .enable("false")) multiplexer_2 (
    .in0(INSTRUCTION), .in1(32'h13), .out(multiplexer_2_out), .sel(PCSel));
  branch_comp branch_comp_1 (.BrEq(BrEq), .BrUn(BrUn), .rs1(rs1Val), .BrLt(BrLt), .rs2(rs2Val));
  Register #(.width(32)) register_1 (.D(multiplexer_2_out), .clk(CLOCK), .Q(INSTRUCTION_DELAY));  // open: en, clr
  Register #(.width(32)) register_2 (.D(PROGRAM_COUNTER), .clk(CLOCK), .Q(PROGRAM_COUNTER_DELAY));  // open: en, clr
  regfile_main RegFile (
    .rs2(INSTRUCTION_DELAY[24:20]), .rd(INSTRUCTION_DELAY[11:7]), .Read_Data_1(rs1Val), .Read_Data_2(rs2Val),
    .ra(ra), .sp(sp), .t0(t0), .t1(t1), .t2(t2), .s0(s0), .s1(s1), .a0(a0), .rs1(INSTRUCTION_DELAY[19:15]),
    .Write_Data(wb), .RegWEn(RegWEn), .clk(CLOCK));
  alu Arithmetic_Logic_Unit (.ALUSel(ALUSel), .Result(ALU_result), .A(A), .B(B));
  Multiplexer #(.width(32), .enable("false")) multiplexer_3 (
    .in0(PROGRAM_COUNTER_DELAY), .in1(rs1Val), .out(A), .sel(ASel));
  Adder #(.width(32)) adder_2 (.a(PROGRAM_COUNTER_DELAY), .b(32'h4), .out(adder_2_out));  // open: cin, cout
  Multiplexer #(.width(32), .enable("false")) multiplexer_4 (.in0(rs2Val), .in1(immediate), .out(B), .sel(BSel));
  // mem_main DMEM: pin names not known; wires that end beside it: ALU_result, rs2Val, CLOCK, MemRW, ReadData
  Multiplexer #(.select(2), .width(32), .enable("false")) multiplexer_5 (
    .in0(adder_2_out), .in1(ALU_result), .in2(ReadData), .out(wb), .sel(WBSel));  // open: in3

  // Other names for the same wires on the sheet: clk = CLOCK; rd[4:0] = INSTRUCTION_DELAY[11:7];
  //   rs1Addr[4:0] = INSTRUCTION_DELAY[19:15]; rs2Addr[4:0] = INSTRUCTION_DELAY[24:20]

  // Notes on the sheet:
  //   Output
  //   IMEM (do **NOT** move this)
  //   Inputs
  //   Inputs/Outputs for testing. Do **NOT** move these.
endmodule
