// Logisim project regfile.circ as structural Verilog: 2 circuits, main circuit main
module main (
  input  [4:0] rs1,
  input  [4:0] rs2,
  input  [4:0] rd,
  input  [31:0] Write_Data,
  input  RegWEn,
  input  clk,
  output [31:0] ra,
  output [31:0] sp,
  output [31:0] t0,
  output [31:0] t1,
  output [31:0] t2,
  output [31:0] s0,
  output [31:0] s1,
  output [31:0] a0,
  output [31:0] Read_Data_1,
  output [31:0] Read_Data_2
);

  wire needwrite_1_needwrite, needwrite_2_needwrite, needwrite_3_needwrite, needwrite_4_needwrite,
       needwrite_5_needwrite, needwrite_6_needwrite, needwrite_7_needwrite, needwrite_8_needwrite;
  wire [31:0] demultiplexer_1_out1, demultiplexer_1_out2, demultiplexer_1_out5, demultiplexer_1_out6,
       demultiplexer_1_out7, demultiplexer_1_out8, demultiplexer_1_out9, demultiplexer_1_out10;

  Demultiplexer #(.select(4), .width(32), .enable("false")) demultiplexer_1 (
    .out1(demultiplexer_1_out1), .out2(demultiplexer_1_out2), .out5(demultiplexer_1_out5),
    .out6(demultiplexer_1_out6), .out7(demultiplexer_1_out7), .out8(demultiplexer_1_out8),
    .out9(demultiplexer_1_out9), .out10(demultiplexer_1_out10), .in(Write_Data), .sel(rd[3:0]));  // open: out0, out3, out4, out11, out12, out13, out14, out15
  Register #(.width(32)) register_1 (
    .D(demultiplexer_1_out1), .en(needwrite_1_needwrite), .clk(clk), .Q(ra));  // open: clr
  needWrite needwrite_1 (.write_en(RegWEn), .index(4'b0001), .write_reg(rd[3:0]), .needWrite(needwrite_1_needwrite));
  Register #(.width(32)) register_2 (
    .D(demultiplexer_1_out2), .en(needwrite_2_needwrite), .clk(clk), .Q(sp));  // open: clr
  needWrite needwrite_2 (.write_en(RegWEn), .index(4'b0010), .write_reg(rd[3:0]), .needWrite(needwrite_2_needwrite));
  Register #(.width(32)) register_3 (
    .D(demultiplexer_1_out5), .en(needwrite_3_needwrite), .clk(clk), .Q(t0));  // open: clr
  needWrite needwrite_3 (.write_en(RegWEn), .index(4'b0101), .write_reg(rd[3:0]), .needWrite(needwrite_3_needwrite));
  Register #(.width(32)) register_4 (
    .D(demultiplexer_1_out6), .en(needwrite_4_needwrite), .clk(clk), .Q(t1));  // open: clr
  needWrite needwrite_4 (.write_en(RegWEn), .index(4'b0110), .write_reg(rd[3:0]), .needWrite(needwrite_4_needwrite));
  Register #(.width(32)) register_5 (
    .D(demultiplexer_1_out7), .en(needwrite_5_needwrite), .clk(clk), .Q(t2));  // open: clr
  needWrite needwrite_5 (.write_en(RegWEn), .index(4'b0111), .write_reg(rd[3:0]), .needWrite(needwrite_5_needwrite));
  Register #(.width(32)) register_6 (
    .D(demultiplexer_1_out8), .en(needwrite_6_needwrite), .clk(clk), .Q(s0));  // open: clr
  needWrite needwrite_6 (.write_en(RegWEn), .index(4'b1000), .write_reg(rd[3:0]), .needWrite(needwrite_6_needwrite));
  Register #(.width(32)) register_7 (
    .D(demultiplexer_1_out9), .en(needwrite_7_needwrite), .clk(clk), .Q(s1));  // open: clr
  needWrite needwrite_7 (.write_en(RegWEn), .index(4'b1001), .write_reg(rd[3:0]), .needWrite(needwrite_7_needwrite));
  Register #(.width(32)) register_8 (
    .D(demultiplexer_1_out10), .en(needwrite_8_needwrite), .clk(clk), .Q(a0));  // open: clr
  needWrite needwrite_8 (.write_en(RegWEn), .index(4'b1010), .write_reg(rd[3:0]), .needWrite(needwrite_8_needwrite));
  Multiplexer #(.select(4), .width(32), .enable("false")) multiplexer_1 (
    .in0({32{1'b0}}), .in1(ra), .in2(sp), .in5(t0), .in6(t1), .in7(t2), .in8(s0), .in9(s1), .in10(a0),
    .out(Read_Data_1), .sel(rs1[3:0]));  // open: in3, in4, in11, in12, in13, in14, in15
  Multiplexer #(.select(4), .width(32), .enable("false")) multiplexer_2 (
    .in0({32{1'b0}}), .in1(ra), .in2(sp), .in5(t0), .in6(t1), .in7(t2), .in8(s0), .in9(s1), .in10(a0),
    .out(Read_Data_2), .sel(rs2[3:0]));  // open: in3, in4, in11, in12, in13, in14, in15

  // Other names for the same wires on the sheet: read_data1[31:0] = Read_Data_1; read_data2[31:0] = Read_Data_2;
  //   read_reg1[4:0] = rs1; read_reg1_3_0[3:0] = rs1[3:0]; read_reg2[4:0] = rs2; read_reg2_3_0[3:0] = rs2[3:0];
  //   write_en = RegWEn; write_reg[4:0] = rd; write_reg3_0[3:0] = rd[3:0]

  // Notes on the sheet:
  //   INPUTS to your circuit
  //   These are DEBUG/TEST outputs from your circuit.
  //   OUTPUTS from your circuit
endmodule

module needWrite (
  input  write_en,
  input  [3:0] index,
  input  [3:0] write_reg,
  output needWrite
);

  wire comparator_1_eq;

  Comparator #(.width(4)) comparator_1 (.a(index), .b(write_reg), .eq(comparator_1_eq));  // open: gt, lt
  and and_1 (needWrite, write_en, comparator_1_eq);
endmodule
